// Logisim project Nova.circ as structural Verilog: 5 circuits, main circuit main
module main (
  output [7:0] out_1
);

  wire clock_1_out, decode_1_regwrite, undriven, undriven_2;
  wire [1:0] decode_1_r1select, decode_1_r2select, decode_1_rtselect, Opcode;
  wire [3:0] registerfile_1_register0, registerfile_1_register0_2, registerfile_1_register1,
       registerfile_1_register1_2, registerfile_1_register2, registerfile_1_register2_2,
       registerfile_1_register3, registerfile_1_register3_2;
  wire [7:0] adder_1_out, alu_1_aluout, MemOut, multiplexer_1_out, R1Out, R2Out, register_1_q;

  Clock clock_1 (.out(clock_1_out));
  Register register_1 (.D(adder_1_out), .clk(clock_1_out), .Q(register_1_q));  // open: en, clr
  Adder adder_1 (.a(8'h1), .b(register_1_q), .out(adder_1_out));  // open: cin, cout
  DataControl datacontrol_1 (.Opcode(Opcode), .Read(undriven), .Write(undriven_2));
  RAM InstructionMem (.addr(register_1_q), .clk(clock_1_out), .dout(out_1));  // open: we, oe, din
  RAM DataMem (.addr(R1Out), .we(undriven), .oe(undriven_2), .clk(clock_1_out), .din(R2Out), .dout(MemOut));
  Decode decode_1 (
    .DecoderIn(out_1), .RtSelect(decode_1_rtselect), .R1Select(decode_1_r1select),
    .R2Select(decode_1_r2select), .Opcode(Opcode), .RegWrite(decode_1_regwrite));
  ALU alu_1 (.Input1(R1Out), .ALUCarry(Opcode[0]), .Input2(R2Out), .ALUOut(alu_1_aluout));
  Multiplexer #(.select(2), .width(8)) multiplexer_1 (
    .in0(alu_1_aluout), .in1(alu_1_aluout), .in2(MemOut), .in3({8{1'b0}}), .out(multiplexer_1_out),
    .sel(Opcode));
  RegisterFile registerfile_1 (
    .Clock(clock_1_out), .ReadReg1(decode_1_r1select), .WriteReg(decode_1_rtselect),
    .ReadReg2(decode_1_r2select), .RegWrite(decode_1_regwrite), .RegDataW(multiplexer_1_out),
    .Register0({registerfile_1_register0_2, registerfile_1_register0}),
    .Register1({registerfile_1_register1_2, registerfile_1_register1}), .RegData1(R1Out), .RegData2(R2Out),
    .Register2({registerfile_1_register2_2, registerfile_1_register2}),
    .Register3({registerfile_1_register3_2, registerfile_1_register3}));
  Hex_Digit_Display hex_digit_display_1 (.value(registerfile_1_register0_2));  // open: dp
  Hex_Digit_Display hex_digit_display_2 (.value(registerfile_1_register1_2));  // open: dp
  Hex_Digit_Display hex_digit_display_3 (.value(registerfile_1_register2_2));  // open: dp
  Hex_Digit_Display hex_digit_display_4 (.value(registerfile_1_register3_2));  // open: dp
  Hex_Digit_Display hex_digit_display_5 (.value(registerfile_1_register0));  // open: dp
  Hex_Digit_Display hex_digit_display_6 (.value(registerfile_1_register1));  // open: dp
  Hex_Digit_Display hex_digit_display_7 (.value(registerfile_1_register2));  // open: dp
  Hex_Digit_Display hex_digit_display_8 (.value(registerfile_1_register3));  // open: dp

  // Notes on the sheet:
  //   Register 0
  //   Register 1
  //   Register 2
  //   Register 3
endmodule

module DataControl (
  input  Read,
  input  [1:0] Opcode,
  input  Write
);

  wire not_1_out;

  not not_1 (not_1_out, Opcode[0]);
  and and_1 (Read, not_1_out, Opcode[1]);
  and and_2 (Write, Opcode[0], Opcode[1]);
endmodule

module Decode (
  input  [7:0] DecoderIn,
  output [1:0] RtSelect,
  output [1:0] R1Select,
  output [1:0] R2Select,
  output [1:0] Opcode,
  output RegWrite
);

  wire and_1_out;

  and and_1 (and_1_out, DecoderIn[6], DecoderIn[7]);
  not not_1 (RegWrite, and_1_out);

  assign Opcode = DecoderIn[7:6];
  assign R1Select = DecoderIn[3:2];
  assign R2Select = DecoderIn[5:4];
  assign RtSelect = DecoderIn[1:0];
endmodule

module RegisterFile (
  input  Clock,
  input  [1:0] ReadReg1,
  input  [1:0] WriteReg,
  input  [1:0] ReadReg2,
  input  RegWrite,
  input  [7:0] RegDataW,
  output [7:0] Register0,
  output [7:0] Register1,
  output [7:0] RegData1,
  output [7:0] RegData2,
  output [7:0] Register2,
  output [7:0] Register3
);

  wire and_1_out, and_2_out, and_3_out, and_4_out, decoder_1_out0, decoder_1_out1, decoder_1_out2,
       decoder_1_out3;

  Decoder #(.select(2)) decoder_1 (
    .out0(decoder_1_out0), .out1(decoder_1_out1), .out2(decoder_1_out2), .out3(decoder_1_out3), .sel(WriteReg));  // open: en
  and and_1 (and_1_out, RegWrite, decoder_1_out0);
  and and_2 (and_2_out, decoder_1_out1, RegWrite);
  and and_3 (and_3_out, decoder_1_out2, RegWrite);
  and and_4 (and_4_out, decoder_1_out3, RegWrite);
  Register register_1 (.D(RegDataW), .en(and_3_out), .clk(Clock), .Q(Register2));  // open: clr
  Register register_2 (.D(RegDataW), .en(and_4_out), .clk(Clock), .Q(Register3));  // open: clr
  Register register_3 (.D(RegDataW), .en(and_1_out), .clk(Clock), .Q(Register0));  // open: clr
  Register register_4 (.D(RegDataW), .en(and_2_out), .clk(Clock), .Q(Register1));  // open: clr
  Multiplexer #(.select(2), .width(8)) multiplexer_1 (
    .in0(Register0), .in1(Register1), .in2(Register2), .in3(Register3), .out(RegData1), .sel(ReadReg1));
  Multiplexer #(.select(2), .width(8)) multiplexer_2 (
    .in0(Register0), .in1(Register1), .in2(Register2), .in3(Register3), .out(RegData2), .sel(ReadReg2));

  // Notes on the sheet:
  //   Write Port
  //   Read Port 1
  //   Read Port 2
endmodule

module ALU (
  input  [7:0] Input1,
  input  ALUCarry,
  input  [7:0] Input2,
  output [7:0] ALUOut
);

  wire [7:0] adder_1_out, subtractor_1_out;

  Adder adder_1 (.a(Input1), .b(Input2), .out(adder_1_out));  // open: cin, cout
  Subtractor subtractor_1 (.a(Input1), .b(Input2), .out(subtractor_1_out));  // open: bin, bout
  Multiplexer #(.width(8)) multiplexer_1 (.in0(adder_1_out), .in1(subtractor_1_out), .out(ALUOut), .sel(ALUCarry));
endmodule
